# Fritzing sketch wiring (saved by Fritzing 0.9.3b)

parts:
  Part1 = RFID-RC522-v2
  WeMos_D1_Mini1 = WeMos D1 Mini
  Squix2 = OLED 0.96" 128x64 I2C SSD1306

nets:
  N1: Part1.SDA, WeMos_D1_Mini1.D8
  N2: Part1.SCK, WeMos_D1_Mini1.D5
  N3: Part1.MOSI, WeMos_D1_Mini1.D7
  N4: Part1.MISO, WeMos_D1_Mini1.D6
  GND: Part1.GND, WeMos_D1_Mini1.G, Squix2.GND
  N5: Part1.RST, WeMos_D1_Mini1.D0
  3.3V: Part1.3.3V, WeMos_D1_Mini1.3V3, Squix2.VCC
  N6: WeMos_D1_Mini1.D1, Squix2.SCL
  N7: WeMos_D1_Mini1.D2, Squix2.SCA

custom parts:
  RFID-RC522-v2: A simple China made RFID-RC522 Reader; do check the pin labels, as this is a MFRC522 based clone.
