# Fritzing sketch wiring (saved by Fritzing 0.9.3b)

parts:
  WeMos_D1_Mini1 = WeMos D1 Mini
  Squix1 = OLED 0.96" 128x64 I2C SSD1306

nets:
  3V3: WeMos_D1_Mini1.3V3, Squix1.VCC
  N1: WeMos_D1_Mini1.D1, Squix1.SCL
  N2: WeMos_D1_Mini1.D2, Squix1.SCA
  N3: WeMos_D1_Mini1.G, Squix1.GND
